# Fritzing sketch Lab 2.PWMButton (saved by Fritzing 0.4.3b)
breadboards: 1

parts:
  Arduino1 = Arduino
  LED1 = Red LED - 5mm
  R1 = Resistor [resistance=220 package=THT]
  S1 = Pushbutton [package=THT]
  R2 = Resistor [resistance=10k package=THT]

nets:
  N1: Arduino1.GND, R1.Pin_1, R2.Pin_1
  N2: Arduino1.D12, S1.leg1, R2.Pin_0
  N3: Arduino1.D9, LED1.anode
  N4: Arduino1.+5V, S1.leg0
  N5: LED1.cathode, R1.Pin_0
