# Fritzing sketch Lab 3.DarknessDetector (saved by Fritzing 0.4.3b)
breadboards: 1

parts:
  Arduino1 = Arduino
  LED1 = Red LED - 5mm
  R1 = Resistor [resistance=220 package=THT]
  R2 = Resistor [resistance=10k package=THT]
  R3 = Photocell (LDR) [package=THT]

nets:
  N1: Arduino1.GND, R1.Pin_1, R3.pin_0
  N2: Arduino1.D9, LED1.anode
  N3: Arduino1.+5V, R2.Pin_1
  N4: Arduino1.A0, R2.Pin_0, R3.pin_1
  N5: LED1.cathode, R1.Pin_0
