# Fritzing sketch LightTheremin1 (saved by Fritzing 0.8.0b)
breadboards: 1

parts:
  Part1 = Arduino Uno (Rev3)
  R1 = Photocell (LDR) [package=THT]
  R2 = Resistor [tolerance=±5% resistance=4.7k package=THT]
  J1 = Piezo Speaker

nets:
  N1: Part1.A0, R1.pin_0, R2.Pin_0
  N2: Part1.GND, R1.pin_1, J1.pin1
  N3: Part1.D9_PWM, J1.pin2
  N4: Part1.5V, R2.Pin_1
